# Fritzing sketch Mini alarme (saved by Fritzing 1.0.4)

parts:
  Part1 = Arduino Uno (Rev3) - ICSP
  Grove1 = Grove OLED 128x96
  J1 = Piezo Speaker
  S1 = Round Pushbutton
  S4 = Magnetic Door Switch [package=reed_switch_plastic]

nets:
  GND: Part1.GND, Grove1.GND, J1.pin1, S1.leg1
  N1: Part1.D8, J1.pin2
  N2: Part1.A4/SDA, Grove1.SDA
  N3: Part1.A5/SCL, Grove1.SCL
  N4: Part1.D2, S1.leg0
  N5: Part1.D3_PWM, S4.2
  5V: Part1.5V, Grove1.VCC
